// Digital circuit CPU.dig as structural Verilog
module CPU (
  input  clk
);

  wire add_2_s, alu_op, B, CI, not_1_out, \reg , undriven, wm, wreg;
  wire [2:0] funct3;
  wire [6:0] funct7, opcode;
  wire [23:0] rd, rs1, rs2;
  wire [31:0] add_1_s, BR_da, BR_db, imm, multiplexer_1_out, multiplexer_2_out, PC_q;
  wire [31:8] undriven_2;

  Multiplexer multiplexer_1 (.sel(undriven), .in_0(add_1_s[0]), .in_1(add_2_s), .out(multiplexer_1_out[0]));
  Register #(.Bits(32)) PC (.D(multiplexer_1_out), .C(clk), .en(1'b1), .Q(PC_q));
  Add #(.Bits(32)) add_1 (.a({undriven_2, 8'h4}), .b(PC_q), .s(add_1_s));  // open: c_i, c_o
  ROM #(.AddrBits(24), .Bits(32)) IM (
    .A(PC_q[23:0]), .sel(1'b1), .D({funct7, rs2[4:0], rs1[4:0], funct3, rd[4:0], opcode}));
  Add add_2 (.a(PC_q[0]), .b(imm[0]), .s(add_2_s));  // open: c_i, c_o
  calc_imm calc_imm_1 (.instr({funct7, rs2[4:0], rs1[4:0], funct3, rd[4:0], opcode}), .imm(imm));  // open: type
  // CU cu_1: pin names not known; wires that end beside it: B, wm, \reg , CI, alu_op, opcode, wreg
  RegisterFile #(.AddrBits(24), .Bits(32)) BR (
    .we(wreg), .Rw(rd), .C(clk), .Ra(rs1), .Rb(rs2), .Da(BR_da), .Db(BR_db));  // open: Din
  Multiplexer #(.Bits(32)) multiplexer_2 (.sel(CI), .in_0(BR_db), .in_1(imm), .out(multiplexer_2_out));
  ULA ula_1 (.op1(BR_da), .op2(multiplexer_2_out));  // open: controle, s
  not not_1 (not_1_out, clk);
  RAMDualPort #(.AddrBits(24), .Bits(32)) MD (.str(wm), .C(not_1_out));  // open: A, Din, ld, D
  // Pins of 1 and 32 bits meet at multiplexer_1_out
  // Pins of 1 and 24 and 32 bits meet at PC_q
  // Pins of 8 and 32 bits meet at {undriven_2, 8'h4}
  // Pins of 1 and 32 bits meet at add_1_s
  // Pins of 5 and 24 bits meet at rd
  // Pins of 5 and 24 bits meet at rs1
  // Pins of 5 and 24 bits meet at rs2
  // Pins of 1 and 32 bits meet at imm
endmodule
