// Digital circuit CU.dig as structural Verilog
module CU (
  input  [5:0] opcode,
  input  [2:0] funct3,
  input  [6:0] funct7,
  output wreg,
  output ula_op,
  output CI,
  output resultSource,
  output wm,
  output B,
  output J
);

  // uni_interna uni_interna_1: pin names not known; wires that end beside it: opcode, funct3, funct7, ula_op, CI
endmodule
